# Fritzing sketch driver (saved by Fritzing 0.8.0b)
breadboards: 1

parts:
  IC1 = IC, DIP package, 28 pins [chip_label=TLC5941]
  J1 = rounded female pin header, 8 pins [form="♀ (female rounded)"]
  J2 = rounded female pin header, 8 pins [form="♀ (female rounded)"]
  J3 = female pin header, 2 pins [form="♀ (female)"]
  J4 = female pin header, 2 pins [form="♀ (female)"]
  J5 = female pin header, 4 pins [form="♀ (female)"]
  J6 = female pin header, 4 pins [form="♀ (female)"]
  R2 = Resistor [tolerance=±5% resistance=500 package=THT]

nets:
  N1: IC1.pin1, J1.pin2
  N2: IC1.pin2, J1.pin3
  N3: IC1.pin3, J1.pin4
  N4: IC1.pin4, J1.pin5
  N5: IC1.pin5, J1.pin6
  N6: IC1.pin6, J1.pin7
  N7: IC1.pin7, J1.pin8
  N8: IC1.pin8, J2.pin1
  N9: IC1.pin9, J2.pin2
  N10: IC1.pin10, J2.pin3
  N11: IC1.pin11, J2.pin4
  N12: IC1.pin12, J2.pin5
  N13: IC1.pin13, J2.pin6
  N14: IC1.pin14, J2.pin7
  N15: IC1.pin15, J2.pin8
  N16: IC1.pin16, IC1.pin22, J3.pin1, J4.pin1, R2.Pin_0
  N17: IC1.pin17, J6.pin2
  N18: IC1.pin18, IC1.pin19, IC1.pin25, J5.pin3, J6.pin3
  N19: IC1.pin20, R2.Pin_1
  N20: IC1.pin21, J3.pin2, J4.pin2
  N21: IC1.pin23, IC1.pin24, J5.pin4, J6.pin4
  N22: IC1.pin26, J5.pin2
  N23: IC1.pin27, J5.pin1, J6.pin1
  N24: IC1.pin28, J1.pin1

notes:
  woozle.org/derby
  digits
  out
  in
